# Fritzing sketch pinout (saved by Fritzing 0.9.3b)

parts:
  Master = ATmega1284 [package=pdpi]
  Slave = ATmega1284 [package=pdpi]
  Confirm_Bn = Pushbutton [package="[THT]"]
  Mode_Switch = Toggle Switch [package=THT]
  Inc/Save_Bn = Pushbutton [package="[THT]"]
  Dec/Reset_Bn = Pushbutton [package="[THT]"]
  Photo-resistor = Photocell (LDR) [package=THT]
  LCD = LCD screen
  Microphone = Microphone
  TemperatureSensor = TMP36 Temperature Sensor [package="TO92 [THT]"]
  LCD_Trimmer = Trimmer Potentiometer [maximum_resistance=10kΩ package=THT]

nets:
  N1: Master.PD0, Slave.PD1
  N2: Master.PD1, Slave.PD0
  N3: Master.PD5, LCD.RS
  N4: Master.PD6, LCD.R/W
  N5: Master.PD7, LCD.E
  N6: Master.PC0, LCD.DB0
  N7: Master.PC1, LCD.DB1
  N8: Master.PC2, LCD.DB2
  N9: Master.PC3, LCD.DB3
  N10: Master.PC4, LCD.DB4
  N11: Master.PC5, LCD.DB5
  N12: Master.PC6, LCD.DB6
  N13: Master.PC7, LCD.DB7
  N14: Master.PA3, Dec/Reset_Bn.Pin_1, Dec/Reset_Bn.Pin_2
  N15: Master.PA2, Inc/Save_Bn.Pin_1, Inc/Save_Bn.Pin_2
  N16: Master.PA1, Confirm_Bn.Pin_1, Confirm_Bn.Pin_2
  N17: Master.PA0, Mode_Switch.COM
  N18: Slave.PA2, TemperatureSensor.Vout
  N19: Slave.PA1, Microphone.pin1
  N20: Slave.PA0, Photo-resistor.pin_1
  N21: LCD.VDD, LCD_Trimmer.wiper

custom parts:
  ATmega1284: AVR 8-bit microcontroller.
